// Logisim project mips-like.circ as structural Verilog
module PROCESSADOR (
  output [31:0] \INSTRUÇÃO 
);

  wire and_1_out, button_1_out, clock_1_out, UC_branch, UC_escreverbr, UC_escrevermemoria, UC_lermemoria,
       UC_multiplexadormemoria, UC_multiplexadorula, UC_registradordestino, UC_ulaop, ula_1_bge;
  wire [3:0] multiplexer_1_out;
  wire [31:0] adder_1_out, adder_2_out, banco_de_registradores_1_r0_d, banco_de_registradores_1_r1_d,
       bit_extender_1_out, multiplexer_2_out, multiplexer_3_out, multiplexer_4_out, PC_q, ram_1_data,
       shifter_1_out, ula_1_ula_out;

  Clock clock_1 (.out(clock_1_out));
  Register #(.width(32)) PC (.D(multiplexer_3_out), .Q(PC_q), .clk(clock_1_out), .clr(button_1_out));  // open: en
  Button button_1 (.out(button_1_out));
  Adder #(.width(32)) adder_1 (.a(32'h4), .b(PC_q), .out(adder_1_out));  // open: cin, cout
  ROM #(.dataWidth(32)) rom_1 (.addr(PC_q[9:2]), .data(\INSTRUÇÃO ));  // open: sel
  UC UC (
    .E3(\INSTRUÇÃO [31]), .E2(\INSTRUÇÃO [30]), .E1(\INSTRUÇÃO [29]), .E0(\INSTRUÇÃO [28]),
    .RegistradorDestino(UC_registradordestino), .Branch(UC_branch), .LerMemoria(UC_lermemoria),
    .MultiplexadorMemoria(UC_multiplexadormemoria), .ULAop(UC_ulaop), .EscreverMemoria(UC_escrevermemoria),
    .MultiplexadorULA(UC_multiplexadorula), .EscreverBR(UC_escreverbr));  // open: Jump
  Multiplexer #(.width(4), .enable("false")) multiplexer_1 (
    .in0(\INSTRUÇÃO [23:20]), .in1(\INSTRUÇÃO [27:24]), .out(multiplexer_1_out), .sel(UC_registradordestino));
  BANCO_DE_REGISTRADORES banco_de_registradores_1 (
    .DATA_WRITE(multiplexer_4_out), .CLK(clock_1_out), .RWR(multiplexer_1_out),
    .R0_D(banco_de_registradores_1_r0_d), .R0(\INSTRUÇÃO [19:16]), .R1_D(banco_de_registradores_1_r1_d),
    .R1(\INSTRUÇÃO [23:20]), .RW(UC_escreverbr), .RESET(button_1_out));
  assign bit_extender_1_out = {{16{\INSTRUÇÃO [15]}}, \INSTRUÇÃO [15:0]};  // Bit_Extender bit_extender_1
  Shifter #(.width(32)) shifter_1 (.in(bit_extender_1_out), .\dist (5'b00010), .out(shifter_1_out));
  Multiplexer #(.width(32), .enable("false")) multiplexer_2 (
    .in0(banco_de_registradores_1_r1_d), .in1(bit_extender_1_out), .out(multiplexer_2_out),
    .sel(UC_multiplexadorula));
  ULA ula_1 (
    .DATA_0(banco_de_registradores_1_r0_d), .DATA_1(multiplexer_2_out), .ULA_OUT(ula_1_ula_out),
    .ULA_OP(UC_ulaop), .BGE(ula_1_bge));
  Multiplexer #(.width(32), .enable("false")) multiplexer_3 (
    .in0(adder_1_out), .in1(adder_2_out), .out(multiplexer_3_out), .sel(and_1_out));
  Adder #(.width(32)) adder_2 (.a(adder_1_out), .b(shifter_1_out), .out(adder_2_out));  // open: cin, cout
  and and_1 (and_1_out, UC_branch, ula_1_bge);
  RAM #(.addrWidth(24), .dataWidth(32), .bus("separate")) ram_1 (
    .addr(ula_1_ula_out[23:0]), .din(banco_de_registradores_1_r1_d), .data(ram_1_data),
    .str(UC_escrevermemoria), .clk(clock_1_out), .ld(UC_lermemoria));  // open: sel, clr
  Multiplexer #(.width(32), .enable("false")) multiplexer_4 (
    .in0(ula_1_ula_out), .in1(ram_1_data), .out(multiplexer_4_out), .sel(UC_multiplexadormemoria));

  // Notes on the sheet:
  //   contents of rom_1 (hex, n*v repeats v):
  //   40ee0000 41ee0010 42ee0020 46ee0000 48ee0000 49ee0000 4bee0004 4fee0001 3eb6001c 47ee0000 3eb70018
  //   4aee0000 3eba000e 1c6b0000 cca0000 1ccf0000 3c00000 53e30000 1cab0000 cc70000 1ccf0000 4c10000
  //   54e40000 1c340000 99c0000 2aea0001 3eeefff1 1c6b0000 cc70000 1ccf0000 5c20000 6e950000 49ee0000
  //   27e70001 3eeeffe7 26e60001 3eeeffe3
  //   REG_0
  //   REG_1
  //   REG_W
  //   DATA_W
  //   BANCO DE REGISTRADORES
  //   REG0_D
  //   REG1_D
  //   ULA
  //   Brach
endmodule

module ULA (
  input  [31:0] DATA_0,
  input  [31:0] DATA_1,
  input  ULA_OP,
  output BGE,
  output [31:0] ULA_OUT
);

  wire comparator_1_eq, comparator_1_gt;
  wire [31:0] adder_1_out, multiplier_1_out;

  Adder #(.width(32)) adder_1 (.a(DATA_0), .b(DATA_1), .out(adder_1_out));  // open: cin, cout
  Multiplier #(.width(32)) multiplier_1 (.a(DATA_0), .b(DATA_1), .out(multiplier_1_out));  // open: cin, cout
  Comparator #(.width(32), .mode("unsigned")) comparator_1 (
    .a(DATA_0), .b(DATA_1), .gt(comparator_1_gt), .eq(comparator_1_eq));  // open: lt
  Multiplexer #(.width(32), .enable("false")) multiplexer_1 (
    .in0(adder_1_out), .in1(multiplier_1_out), .out(ULA_OUT), .sel(ULA_OP));
  or or_1 (BGE, comparator_1_gt, comparator_1_eq);
endmodule

module UC (
  input  E3,
  input  E2,
  input  E1,
  input  E0,
  output RegistradorDestino,
  output Jump,
  output Branch,
  output LerMemoria,
  output MultiplexadorMemoria,
  output ULAop,
  output EscreverMemoria,
  output MultiplexadorULA,
  output EscreverBR
);

  wire and_1_out, and_2_out, and_3_out, and_7_out, and_8_out, and_9_out, and_10_out, and_11_out, not_1_out,
       not_2_out, not_3_out, not_4_out, not_5_out, not_6_out, not_7_out, not_8_out, not_9_out, not_10_out,
       not_11_out, not_12_out, not_13_out, not_14_out, not_15_out, not_16_out, not_17_out, not_18_out,
       not_19_out, not_20_out, not_21_out, not_22_out;

  not not_1 (not_1_out, E3);
  not not_2 (not_2_out, E2);
  and and_1 (and_1_out, not_1_out, not_2_out, not_3_out);
  not not_3 (not_3_out, E0);
  not not_4 (not_4_out, E1);
  and and_2 (and_2_out, E2, E0);
  and and_3 (and_3_out, E3, E2);
  and and_4 (Jump, E2, E1, E0);
  and and_5 (Branch, E1, E0);
  not not_5 (not_5_out, E3);
  not not_6 (not_6_out, E1);
  not not_7 (not_7_out, E3);
  not not_8 (not_8_out, E1);
  not not_9 (not_9_out, E2);
  and and_6 (ULAop, not_9_out, E0);
  not not_10 (not_10_out, E3);
  not not_11 (not_11_out, E0);
  not not_12 (not_12_out, E2);
  and and_7 (and_7_out, not_12_out, E1, not_13_out);
  not not_13 (not_13_out, E0);
  not not_14 (not_14_out, E3);
  and and_8 (and_8_out, not_14_out, E2, not_15_out);
  not not_15 (not_15_out, E1);
  not not_16 (not_16_out, E3);
  and and_9 (and_9_out, not_16_out, E2, not_17_out);
  not not_17 (not_17_out, E0);
  not not_18 (not_18_out, E1);
  and and_10 (and_10_out, E2, not_18_out, not_19_out);
  not not_19 (not_19_out, E0);
  not not_20 (not_20_out, E2);
  and and_11 (and_11_out, not_20_out, not_21_out);
  not not_21 (not_21_out, E0);
  not not_22 (not_22_out, E1);
  or or_1 (RegistradorDestino, and_1_out, not_4_out, and_2_out, and_3_out);
  and and_12 (LerMemoria, not_5_out, E2, not_6_out, E0);
  and and_13 (MultiplexadorMemoria, not_7_out, E2, not_8_out, E0);
  and and_14 (EscreverMemoria, not_10_out, E2, E1, not_11_out);
  or or_2 (MultiplexadorULA, and_7_out, and_8_out, and_9_out, and_10_out);
  or or_3 (EscreverBR, and_11_out, not_22_out);
endmodule

module BANCO_DE_REGISTRADORES (
  input  [31:0] DATA_WRITE,
  input  [3:0] R0,
  input  [3:0] R1,
  input  CLK,
  input  [3:0] RWR,
  input  RESET,
  input  RW,
  output [31:0] R0_D,
  output [31:0] R1_D
);

  wire demultiplexer_1_out0, demultiplexer_1_out1, demultiplexer_1_out2, demultiplexer_1_out3,
       demultiplexer_1_out4, demultiplexer_1_out5, demultiplexer_1_out6, demultiplexer_1_out7,
       demultiplexer_1_out8, demultiplexer_1_out9, demultiplexer_1_out10, demultiplexer_1_out11,
       demultiplexer_1_out12, demultiplexer_1_out13, demultiplexer_1_out14, demultiplexer_1_out15;
  wire [31:0] register_1_q, register_2_q, register_3_q, register_4_q, register_5_q, register_6_q,
       register_7_q, register_8_q, register_9_q, register_10_q, register_11_q, register_12_q, register_13_q,
       register_14_q, register_15_q, register_16_q;

  Demultiplexer #(.select(4), .enable("false")) demultiplexer_1 (
    .out0(demultiplexer_1_out0), .out1(demultiplexer_1_out1), .out2(demultiplexer_1_out2),
    .out3(demultiplexer_1_out3), .out4(demultiplexer_1_out4), .out5(demultiplexer_1_out5),
    .out6(demultiplexer_1_out6), .out7(demultiplexer_1_out7), .out8(demultiplexer_1_out8),
    .out9(demultiplexer_1_out9), .out10(demultiplexer_1_out10), .out11(demultiplexer_1_out11),
    .out12(demultiplexer_1_out12), .out13(demultiplexer_1_out13), .out14(demultiplexer_1_out14),
    .out15(demultiplexer_1_out15), .in(RW), .sel(RWR));
  Register #(.width(32)) register_1 (
    .D(DATA_WRITE), .en(demultiplexer_1_out0), .Q(register_1_q), .clk(CLK), .clr(RESET));
  Register #(.width(32)) register_2 (
    .D(DATA_WRITE), .en(demultiplexer_1_out1), .Q(register_2_q), .clk(CLK), .clr(RESET));
  Register #(.width(32)) register_3 (
    .D(DATA_WRITE), .en(demultiplexer_1_out2), .Q(register_3_q), .clk(CLK), .clr(RESET));
  Register #(.width(32)) register_4 (
    .D(DATA_WRITE), .en(demultiplexer_1_out3), .Q(register_4_q), .clk(CLK), .clr(RESET));
  Register #(.width(32)) register_5 (
    .D(DATA_WRITE), .en(demultiplexer_1_out4), .Q(register_5_q), .clk(CLK), .clr(RESET));
  Register #(.width(32)) register_6 (
    .D(DATA_WRITE), .en(demultiplexer_1_out5), .Q(register_6_q), .clk(CLK), .clr(RESET));
  Register #(.width(32)) register_7 (
    .D(DATA_WRITE), .en(demultiplexer_1_out6), .Q(register_7_q), .clk(CLK), .clr(RESET));
  Register #(.width(32)) register_8 (
    .D(DATA_WRITE), .en(demultiplexer_1_out7), .Q(register_8_q), .clk(CLK), .clr(RESET));
  Register #(.width(32)) register_9 (
    .D(DATA_WRITE), .en(demultiplexer_1_out8), .Q(register_9_q), .clk(CLK), .clr(RESET));
  Register #(.width(32)) register_10 (
    .D(DATA_WRITE), .en(demultiplexer_1_out9), .Q(register_10_q), .clk(CLK), .clr(RESET));
  Register #(.width(32)) register_11 (
    .D(DATA_WRITE), .en(demultiplexer_1_out10), .Q(register_11_q), .clk(CLK), .clr(RESET));
  Register #(.width(32)) register_12 (
    .D(DATA_WRITE), .en(demultiplexer_1_out11), .Q(register_12_q), .clk(CLK), .clr(RESET));
  Register #(.width(32)) register_13 (
    .D(DATA_WRITE), .en(demultiplexer_1_out12), .Q(register_13_q), .clk(CLK), .clr(RESET));
  Register #(.width(32)) register_14 (
    .D(DATA_WRITE), .en(demultiplexer_1_out13), .Q(register_14_q), .clk(CLK), .clr(RESET));
  Register #(.width(32)) register_15 (
    .D(DATA_WRITE), .en(demultiplexer_1_out14), .Q(register_15_q), .clk(CLK), .clr(RESET));
  Register #(.width(32)) register_16 (
    .D(DATA_WRITE), .en(demultiplexer_1_out15), .Q(register_16_q), .clk(CLK), .clr(RESET));
  Multiplexer #(.select(4), .width(32), .disabled(0), .enable("false")) multiplexer_1 (
    .in0(register_1_q), .in1(register_2_q), .in2(register_3_q), .in3(register_4_q), .in4(register_5_q),
    .in5(register_6_q), .in6(register_7_q), .in7(register_8_q), .in8(register_9_q), .in9(register_10_q),
    .in10(register_11_q), .in11(register_12_q), .in12(register_13_q), .in13(register_14_q),
    .in14(register_15_q), .in15(register_16_q), .out(R0_D), .sel(R0));
  Multiplexer #(.select(4), .width(32), .enable("false")) multiplexer_2 (
    .in0(register_1_q), .in1(register_2_q), .in2(register_3_q), .in3(register_4_q), .in4(register_5_q),
    .in5(register_6_q), .in6(register_7_q), .in7(register_8_q), .in8(register_9_q), .in9(register_10_q),
    .in10(register_11_q), .in11(register_12_q), .in12(register_13_q), .in13(register_14_q),
    .in14(register_15_q), .in15(register_16_q), .out(R1_D), .sel(R1));

  // Notes on the sheet:
  //   T0
  //   T1
  //   T2
  //   T3
  //   T4
  //   T5
  //   T6
  //   S0
  //   S1
  //   S2
  //   S3
  //   S4
  //   S5
endmodule

module ShiftLeft2 (
  input  [31:0] E0,
  input  [31:0] E1,
  output [31:0] S1
);

  Shifter #(.width(28)) shifter_1 (.in({2'b00, E0[25:0]}), .\dist (5'b00010), .out(S1[27:0]));

  assign S1[31:28] = E1[31:28];
endmodule

module EstendeBits (
  input  [31:0] Epasso,
  input  [31:0] EInstrucao,
  output [31:0] SBranch
);

  wire [31:0] bit_extender_1_out, shifter_1_out;

  Adder #(.width(32)) adder_1 (.a(Epasso), .b(shifter_1_out), .out(SBranch));  // open: cin, cout
  Shifter #(.width(32)) shifter_1 (.in(bit_extender_1_out), .\dist (5'b00010), .out(shifter_1_out));
  assign bit_extender_1_out = {{16{EInstrucao[15]}}, EInstrucao[15:0]};  // Bit_Extender bit_extender_1
endmodule

module negador (
  input  [15:0] in_1,
  input  [15:0] in_2,
  output [15:0] out_3,
  output [15:0] out_4
);

  Negator #(.width(16)) negator_1 (.in(in_1), .out(out_3));
  Negator #(.width(16)) negator_2 (.in(in_2), .out(out_4));

  // Notes on the sheet:
  //   Volta
  //   Ida
endmodule
